// Logisim project ALU3.circ as structural Verilog
module main (
  input  in_1,
  input  in_2
);
endmodule

module xor_circuit (
  input  [31:0] a,
  input  [31:0] b,
  output [31:0] res_low
);

  assign res_low = a ^ b;  // XOR_Gate xor_1, 32 bits wide
endmodule

module or_circuit (
  input  [31:0] a,
  input  [31:0] b,
  output [31:0] res_low
);

  assign res_low = a | b;  // OR_Gate or_1, 32 bits wide
endmodule

module and_circuit (
  input  [31:0] a,
  input  [31:0] b,
  output [31:0] res_low
);

  assign res_low = a & b;  // AND_Gate and_1, 32 bits wide
endmodule

module add_circuit (
  input  [31:0] a,
  input  [31:0] b,
  input  [3:0] aluop,
  input  output_inverted,
  input  output_inc,
  input  clk,
  input  rst,
  output [31:0] res_low,
  output [31:0] res_high
);

  wire adder_1_cout;

  Adder #(.width(32)) adder_1 (.a(a), .b(b), .out(res_low), .cin(1'b0), .cout(adder_1_cout));
  assign res_high = {{31{1'b0}}, adder_1_cout};  // Bit_Extender bit_extender_1
endmodule

module sub_circuit (
  input  [31:0] a,
  input  [31:0] b,
  input  [3:0] aluop,
  input  output_inverted,
  input  output_inc,
  input  clk,
  input  rst,
  output [31:0] res_low,
  output [31:0] res_high
);

  wire subtractor_1_bout;

  Subtractor #(.width(32)) subtractor_1 (.a(a), .b(b), .out(res_low), .bin(1'b0), .bout(subtractor_1_bout));
  assign res_high = {{31{1'b0}}, subtractor_1_bout};  // Bit_Extender bit_extender_1
endmodule
